# Fritzing sketch SF51-Living-Window-v1 (saved by Fritzing 0.9.3b)
breadboards: 1

parts:
  U2 = NodeMCU V3.0
  5_V = Power Jack [package=power_jack_pth_lock]
  Motor_1 = DC Motor
  Motor2 = DC Motor
  IC2 = L293D [package=THT]
  D1 = Schottky Diode [part_number=1N5817 package="300 mil [THT]"]
  IC3 = L293D [package=THT]
  12_V1 = Power Jack [package=power_jack_pth_lock]
  U3 = V_REG_MC33269 [package=dpak]
  Motor3 = DC Motor
  U4 = XPORT [package=xport]

nets:
  N1: U2.D4, IC3.Enable_1
  N2: U2.3V3, IC2.+Vmotor, IC2.Enable_2, IC3.+Vmotor
  N3: U2.GND#6, U2.GND#13, U2.GND#16, U2.GND#33, 5_V.GNDBREAK
  VIN: U2.Vin, 5_V.GND
  N4: Motor_1.pin_1, IC3.Out_3_(_Controlled_by_Enable_2_)
  N5: Motor_1.pin_2, Motor2.pin_1, IC2.Out_4_(_Controlled_by_Enable_2_)
  N6: Motor2.pin_2, IC3.Out_2_(_Controlled_by_Enable_1_)
  N7: IC2.Out_1_(_Controlled_by_Enable_1_), Motor3.pin_2
  N8: IC2.Out_2_(_Controlled_by_Enable_1_), Motor3.pin_1
  N9: IC2.In_3, D1.anode
  N10: IC2.+V, IC3.+V
  N11: D1.cathode, U4.RTS
  N12: 12_V1.GND, U3.IN
  N13: 12_V1.GNDBREAK, U3.OUT

custom parts:
  NodeMCU V3.0: ESP8266 based NodeMCU
