# Fritzing sketch SF51-Window-Wires-v0.2 (saved by Fritzing 0.9.3b)
breadboards: 2

parts:
  U2 = NodeMCU V3.0
  5_V = Power Jack [package=power_jack_pth_lock]
  Door_slider1 = DC Motor
  IC2 = L293D [package=THT]
  Part1 = LilyPad LED
  Door_slider2 = DC Motor
  Part2 = LilyPad LED
  Part3 = LilyPad LED
  Part4 = LilyPad LED
  Part5 = LilyPad LED
  Part6 = LilyPad LED
  D3 = Schottky Diode [part_number=1N5817 package="300 mil [THT]"]
  D4 = Schottky Diode [part_number=1N5817 package="300 mil [THT]"]
  Q8 = NPN-Transistor [package="SOT-23 [SMD]"]
  Q9 = NPN-Transistor [package="SOT-23 [SMD]"]  # not connected
  D5 = Schottky Diode [part_number=1N5817 package="300 mil [THT]"]  # not connected
  D6 = Schottky Diode [part_number=1N5817 package="300 mil [THT]"]
  D7 = Schottky Diode [part_number=1N5817 package="300 mil [THT]"]
  Q10 = PNP-Transistor [package="TO92 [THT]"]  # not connected
  U3 = NodeMCU V3.0
  IC3 = L293D [package=THT]
  LED1 = LED - 5mm [color="Red (633nm)" package="5 mm [THT]"]
  LED2 = LED - 5mm [color="Red (633nm)" package="5 mm [THT]"]
  R1 = Resistor [tolerance=±5% resistance=220 package=THT]
  R2 = Resistor [tolerance=±5% resistance=220 package=THT]
  Part7 = LilyPad LED  # not connected
  Part8 = LilyPad LED  # not connected
  Part9 = LilyPad LED
  Part10 = LilyPad LED  # not connected
  Part11 = LilyPad LED  # not connected
  Part12 = LilyPad LED  # not connected

nets:
  N1: U2.GND#6, U2.GND#16, U2.GND#33, 5_V.GNDBREAK, IC2.0V
  VIN: U2.Vin, 5_V.GND, IC2.+Vmotor, IC2.+V
  N2: Door_slider1.pin_2, Part4.+, Part5.+, Part6.+, D3.cathode, Q8.2
  N3: IC2.Out_1_(_Controlled_by_Enable_1_), D7.anode
  N4: IC2.Out_2_(_Controlled_by_Enable_1_), D6.anode
  N5: IC2.Out_3_(_Controlled_by_Enable_2_), Part1.-, Door_slider2.pin_2, Part2.-, Part3.-
  N6: IC2.Out_4_(_Controlled_by_Enable_2_), Part5.-, Part6.-, Part9.-
  N7: Part1.+, Part2.+, Part3.+, D4.cathode, Q8.0
  N8: Door_slider2.pin_1, Part4.-
  N9: U3.D0, IC3.Enable_1
  N10: U3.D1, IC3.In_1
  N11: U3.D2, IC3.In_2
  N12: U3.3V3, IC3.+V
  N13: U3.GND#6, U3.GND#13, U3.GND#16, U3.GND#33, IC3.0V
  N14: U3.D5, IC3.Enable_2
  N15: U3.D6, IC3.In_3
  N16: U3.D7, IC3.In_4
  N17: LED1.cathode, R1.Pin_0
  N18: LED2.cathode, R2.Pin_1

notes:
  (+ / -)
  (+)
  (-)
  2nd M *1
  1st M
  2nd M *2
  (0)
  Light only
  (+) X
  (-) X
  (- / +)

custom parts:
  NodeMCU V3.0: ESP8266 based NodeMCU
